# Fritzing sketch ArduinoDojoShield (saved by Fritzing 0.9.1b)
breadboards: 1

parts:
  Part1 = Arduino Uno (Rev3)
  R1 = Rotary Potentiometer (Large) [maximum_resistance=10kΩ package=THT]
  R2 = Resistor [tolerance=±5% resistance=10k package=THT]
  R3 = Photocell (LDR) [package=THT]
  U1 = 74HC595 SMD [package="SO16 [SMD]"]
  LED1 = RGB LED (com. cathode, rgb) [package="5 mm [THT]"]
  R6 = Resistor [tolerance=±5% resistance=330 package=THT]
  R4 = Resistor [tolerance=±5% resistance=330 package=THT]
  R5 = Resistor [tolerance=±5% resistance=330 package=THT]
  S1 = Pushbutton [package="[THT]"]
  S2 = Pushbutton [package="[THT]"]
  J1 = Basic Servo
  J2 = Basic Servo
  R7 = Resistor [tolerance=±5% resistance=330 package=THT]
  R8 = Resistor [tolerance=±5% resistance=330 package=THT]
  R9 = Resistor [tolerance=±5% resistance=330 package=THT]
  R10 = Resistor [tolerance=±5% resistance=330 package=THT]
  R11 = Resistor [tolerance=±5% resistance=330 package=THT]
  R12 = Resistor [tolerance=±5% resistance=330 package=THT]
  R13 = Resistor [tolerance=±5% resistance=330 package=THT]
  7_Segment1 = 7 Segment Display
  R6_2 = Resistor [tolerance=±5% resistance=330 package=THT]
  J3 = female pin header, 3 pins [form="♀ (female)"]

nets:
  N1: Part1.A0, R1.wiper
  N2: Part1.A1, R2.Pin_0, R3.pin_1
  N3: Part1.D8, S2.Pin_1, S2.Pin_2
  servo1: Part1.D9_PWM, J1.pulse
  servo2: Part1.D10_PWM/SS, J2.pulse
  N4: Part1.D11_PWM/MOSI, U1.ST_CP
  N5: Part1.D12/MISO, U1.SH_CP
  N6: Part1.D13/SCK, U1.DS
  N7: Part1.D0/RX, J3.pin1
  N8: Part1.D1/TX, J3.pin2
  N9: Part1.D3_PWM, R4.Pin_0
  N10: Part1.D5_PWM, R5.Pin_0
  N11: Part1.D6_PWM, R6.Pin_0
  N12: Part1.D7, S1.Pin_1, S1.Pin_2
  5V: Part1.5V, R1.leg2, R2.Pin_1, U1.MR, U1.VCC, J1.vcc, J2.vcc
  GND: Part1.GND, R1.leg1, R3.pin_0, U1.GND, U1.OE, LED1.common_cathode, S1.Pin_3, S1.Pin_4, S2.Pin_3, S2.Pin_4, J1.gnd, J2.gnd, 7_Segment1.common_cathode, J3.pin3
  N13: U1.Q1, R7.Pin_0
  N14: U1.Q2, R8.Pin_0
  N15: U1.Q3, R9.Pin_0
  N16: U1.Q4, R10.Pin_0
  N17: U1.Q5, R11.Pin_0
  N18: U1.Q6, R12.Pin_0
  N19: U1.Q7, R13.Pin_0
  N20: U1.Q0, R6_2.Pin_0
  N21: LED1.red_anode, R4.Pin_1
  N22: LED1.green_anode, R6.Pin_1
  N23: LED1.blue_anode, R5.Pin_1
  N24: R7.Pin_1, 7_Segment1.Segment_A#1
  N25: R8.Pin_1, 7_Segment1.Segment_F
  N26: R9.Pin_1, 7_Segment1.Segment_E
  N27: R10.Pin_1, 7_Segment1.Segment_D
  N28: R11.Pin_1, 7_Segment1.Segment_C
  N29: R12.Pin_1, 7_Segment1.Segment_B
  N30: R13.Pin_1, 7_Segment1.Segment_A#10
  N31: 7_Segment1.Segment_DP, R6_2.Pin_1
